# Fritzing sketch Luci_conexións (saved by Fritzing 0.9.10b)
breadboards: 1

parts:
  Part1 = Arduino Nano (Rev3.0) (ICSP)
  Driver1 = 28BYJ-48 Driver Module [part_number=ULN2003 package=THT]
  Driver2 = 28BYJ-48 Driver Module [part_number=ULN2003 package=THT]
  passive_buzzer1 = Passive buzzer [package=THT]
  Keypad1 = EscornaKeypad [package=THT]
  SM1 = 28BYJ-48 Stepper Motor [part_number=28BYJ-48]
  SM2 = 28BYJ-48 Stepper Motor [part_number=28BYJ-48]
  Part2 = NeoPixel [part_number=WS2812B]
  S1 = SWITCH_SPDT [package=kps-1290]
  PB1 = Powerbank-DIY [package=battery-18650]

nets:
  GND: Part1.GND, Driver1.GND, Driver2.GND, passive_buzzer1.pin2, Keypad1.GND, Part2.GND, PB1.GND
  N1: Part1.D2, passive_buzzer1.pin1
  N2: Part1.D4, Driver1.IN1
  N3: Part1.D5, Driver1.IN2
  N4: Part1.D6, Driver1.IN3
  N5: Part1.D7, Driver1.IN4
  N6: Part1.D8, Driver2.IN1
  N7: Part1.D9, Driver2.IN2
  N8: Part1.D10, Driver2.IN3
  N9: Part1.D11/MOSI, Driver2.IN4
  N10: Part1.D12/MISO, Part2.IN
  5V: Part1.5V, Driver1.Vmotor, Driver2.Vmotor, Part2.VDD, S1.S
  N11: Part1.A0, Keypad1.SIG
  N12: Driver1.blue-pin, SM1.blue-pin
  N13: Driver1.pink-pin, SM1.pink-pin
  N14: Driver1.yellow-pin, SM1.yellow-pin
  N15: Driver1.orange-pin, SM1.orange-pin
  N16: Driver1.red-pin, SM1.red-pin
  N17: Driver2.blue-pin, SM2.blue-pin
  N18: Driver2.pink-pin, SM2.pink-pin
  N19: Driver2.yellow-pin, SM2.yellow-pin
  N20: Driver2.orange-pin, SM2.orange-pin
  N21: Driver2.red-pin, SM2.red-pin
  N22: S1.P, PB1.5V

notes:
  RIGHT STEPPER MOTOR
  LEFT STEPPER MOTOR
  BUZZER
  NEOPIXEL
  KEYPAD
  RIGHT DRIVER
  LEFT DRIVER
  5V
  ESCORNABOT
  LUCI

custom parts:
  28BYJ-48 Driver Module: ULN2003 Driver Module for the 28BYJ-48 Unipolar Stepper Motor LED A - Blue wire - Bottom coil left LED B - Pink wire - Top coil left LED C - Yellow wire - Bottom coil right LED D - Orange wire - Top coil right Common rail - red Connector pins: blue - pink - yellow - orange - red Control pins - IN1 to IN4 Power pins - GND & Vmotor (5-12V) On/Off jumper (if removed, power to motor is cut).
  Passive buzzer: Passive buzzer 12 mm, 3-5 V
  EscornaKeypad: Keypad with 5 push buttons for the Escornabot robot: escornabot.org.
  28BYJ-48 Stepper Motor: Unipolar Stepper Motor 28BYJ-48 Top coil - pink & orange Bottom coil - blue & yellow Common rail - red Connector pins: blue - pink - yellow - orange - red
  NeoPixel: Single unit of a NeoPixel, based on the bright RGB LED WS2812B. These ultra-bright LEDs have a constant-current driver cooked right into the LED package! The pixels are chainable - so you only need 1 pin/wire to control as many LEDs as you like.
  Powerbank-DIY: Powerbank-DIY (do it yourself) with one 18650 Li-ion battery cell and modded with dupont cables.
